// Logisim project Elevator.circ as structural Verilog
module main (
  input  reset,
  input  [3:0] cerere,
  input  in_3,
  input  om,
  input  sg,
  input  in_6,
  output [3:0] anod,
  output [3:0] count,
  output check_destination,
  output [3:0] prev_state,
  output empty,
  output [3:0] data_out,
  output full
);

  wire clk_nexys_out, comparator_1_output, divizor_frecv_timer1_1_d, divizor_frecv_timer3_1_d,
       mux_sel_viteza_1_output, not_1_out, numarator_zecimal_reversibil_1_led_om,
       numarator_zecimal_reversibil_1_led_sg, ok_cerere_out, timer5_usi_deschise_1_output;
  wire [3:0] fifo_1_num_elem;
  wire [6:0] seven_segment_2_digits_1_catod;

  Clock clk_nexys (.out(clk_nexys_out));
  Button ok_cerere (.out(ok_cerere_out));
  divizor_frecv_timer1 divizor_frecv_timer1_1 (.CLK(clk_nexys_out), .reset(reset), .D(divizor_frecv_timer1_1_d));
  divizor_frecv_timer3 divizor_frecv_timer3_1 (.CLK(clk_nexys_out), .reset(reset), .D(divizor_frecv_timer3_1_d));
  not not_1 (not_1_out, check_destination);
  timer5_usi_deschise timer5_usi_deschise_1 (
    .reset5(not_1_out), .clk5(clk_nexys_out), .enable(check_destination),
    .\output (timer5_usi_deschise_1_output));
  fifo fifo_1 (
    .clk(clk_nexys_out), .reset(reset), .enr(timer5_usi_deschise_1_output), .enw(ok_cerere_out),
    .data_in(cerere), .ext_or_int(in_3), .data_out(data_out), .prev_state(prev_state), .empty(empty),
    .full(full), .num_elem(fifo_1_num_elem));
  mux_sel_viteza mux_sel_viteza_1 (
    .input1(divizor_frecv_timer1_1_d), .input2(divizor_frecv_timer3_1_d), .s(in_6),
    .\output (mux_sel_viteza_1_output));
  comparator comparator_1 (.A(data_out), .B(prev_state), .\output (comparator_1_output));
  numarator_zecimal_reversibil numarator_zecimal_reversibil_1 (
    .dir(comparator_1_output), .reset(reset), .clk(mux_sel_viteza_1_output), .load_value(prev_state),
    .destination(data_out), .enable(fifo_1_num_elem), .om(om), .sg(sg), .count(count),
    .check_destination(check_destination), .led_om(numarator_zecimal_reversibil_1_led_om),
    .led_sg(numarator_zecimal_reversibil_1_led_sg));
  seven_segment_2_digits seven_segment_2_digits_1 (
    .\input (count), .clock(clk_nexys_out), .dir(comparator_1_output), .anod(anod),
    .catod(seven_segment_2_digits_1_catod));
  LED led_om (.in(numarator_zecimal_reversibil_1_led_om));
  LED led_sg (.in(numarator_zecimal_reversibil_1_led_sg));
  _7_Segment_Display afisor (
    .g(seven_segment_2_digits_1_catod[0]), .f(seven_segment_2_digits_1_catod[1]),
    .a(seven_segment_2_digits_1_catod[6]), .b(seven_segment_2_digits_1_catod[5]),
    .e(seven_segment_2_digits_1_catod[2]), .d(seven_segment_2_digits_1_catod[3]),
    .c(seven_segment_2_digits_1_catod[4]));  // open: dp
endmodule

// VHDL entity lift, as the project stores it:
LIBRARY ieee;
USE ieee.std_logic_1164.all;

ENTITY lift IS
PORT (
	cerere: in std_logic_vector(3 downto 0);
  	ok_cerere_enw: in std_logic;
  	ext_or_int: in std_logic;		-- '1' -> interior, '0' -> exterior
  	om: in std_logic;
  	sg: in std_logic;
  	viteza: in std_logic;
  	clk_nexys: in std_logic;
  	afisor_anod: out std_logic_vector(3 downto 0);
  	afisor_catod: out std_logic_vector(6 downto 0);
  	led_om: out std_logic;
  	led_sg: out std_logic;
  	RESET: in std_logic
    );
END lift;


ARCHITECTURE arch_lift OF lift IS

--componente
component fifo is
port(
    clk : in std_logic;
    reset : in std_logic;
    enr : in std_logic;   
    ok_cerere_enw: in std_logic;   
    data_in : in std_logic_vector (3 downto 0);  
    ext_or_int: in std_logic;  
    data_out : out std_logic_vector(3 downto 0);    
    prev_state : out std_logic_vector(3 downto 0);   
    empty : out std_logic;
    full : out std_logic;
    num_elem: out std_logic_vector (3 downto 0)
  );
end component fifo;

component numarator_zecimal_reversibil is
    port (
        dir: in std_logic;
        count: out std_logic_vector(3 downto 0);
        reset: in std_logic;
        clk: in std_logic;
        load_value: in std_logic_vector(3 downto 0);
        check_destination: out std_logic;
        destination: in std_logic_vector(3 downto 0);
        enable: in std_logic_vector(3 downto 0);
        om: in std_logic;
        sg: in std_logic;
        led_om: out std_logic;
        led_sg: out std_logic
    );
end component numarator_zecimal_reversibil;

component comparator is
    port (
        A, B: in std_logic_vector(3 downto 0);
        output: out std_logic
    );
end component comparator;

component seven_segment_2_digits IS
  PORT (
  	input: in std_logic_vector(3 downto 0);
  	anod: out std_logic_vector(3 downto 0);
  	catod: out std_logic_vector(6 downto 0);
  	clock: in std_logic;
  	dir: in std_logic
    );
END component seven_segment_2_digits;

component timer5_usi_deschise IS
  PORT (
  	reset5: in std_logic;
  	clk5: in std_logic;
  	enable: in std_logic;
  	output: out std_logic
    );
END component timer5_usi_deschise;

component divizor_frecv_timer1 is 
port( 
    CLK : in std_logic;
    reset: in std_logic;
    D : out std_logic
);
end component divizor_frecv_timer1;

component divizor_frecv_timer3 is 
port( 

    CLK : in std_logic;
    reset: in std_logic;
    D : out std_logic
);
end component divizor_frecv_timer3;

component mux_sel_viteza IS
  PORT (
 	input1, input2: in std_logic;
 	s: in std_logic;
 	output: out std_logic
    );
END component mux_sel_viteza;
--semnale intermediare
signal output_timer5: std_logic:='1';
signal fifo_data_out: std_logic_vector(3 downto 0) := "0000";
signal fifo_prev_state: std_logic_vector(3 downto 0) := "0000";
signal empty_s: std_logic;
signal full_s: std_logic;
signal num_elem_s: std_logic_vector(3 downto 0):= "0000";
signal check_dest: std_logic := '1';
signal output_comparator: std_logic :='1';
signal clk_1: std_logic:=clk_nexys;
signal clk_3: std_logic:=clk_nexys;
signal clk_divizat:std_logic;
signal count_afisor: std_logic_vector(3 downto 0):= "0000";
BEGIN
--legarea componentelor top level structural
	fifoo: fifo port map(clk_nexys, reset, output_timer5, ok_cerere_enw, cerere, ext_or_int, fifo_data_out, fifo_prev_state, empty_s, full_s, num_elem_s);
	timer5_usa: timer5_usi_deschise port map(reset, clk_nexys, check_dest, output_timer5);
	comparator_etaje: comparator port map(fifo_data_out, fifo_prev_state, output_comparator);
	divizor1: divizor_frecv_timer1 port map(clk_nexys, reset, clk_1);
	divizor3: divizor_frecv_timer3 port map(clk_nexys, reset, clk_3);
	mux: mux_sel_viteza  port map(clk_1, clk_3, viteza, clk_divizat);
	numarator_reversibil: numarator_zecimal_reversibil port map(output_comparator, count_afisor, reset, clk_divizat, fifo_prev_state, check_dest, fifo_data_out, num_elem_s, om, sg, led_om, led_sg);
	afisaj: seven_segment_2_digits port map(count_afisor, afisor_anod, afisor_catod, clk_nexys, output_comparator);
END arch_lift;

library IEEE;
use IEEE.STD_LOGIC_1164.ALL;
use IEEE.NUMERIC_STD.ALL;

entity fifo is
port(
    clk : in std_logic;
    reset : in std_logic;
    enr : in std_logic;   
    enw : in std_logic;   
    data_in : in std_logic_vector (3 downto 0);   
    ext_or_int: in std_logic; 
    data_out : out std_logic_vector(3 downto 0);    
    prev_state : out std_logic_vector(3 downto 0);   
    empty : out std_logic;
    full : out std_logic;
    num_elem: out std_logic_vector (3 downto 0)
  );
end entity fifo;

architecture arch_fifo of fifo is
  type memory_type is array (0 to 13) of std_logic_vector(3 downto 0);
  signal memory : memory_type := (others => (others => '0'));  --memory pentru fifo
  signal readptr, writeptr : integer range 0 to 14 := 0;
  signal is_num_elem: integer range 0 to 14;
  signal is_full: std_logic := '0';
  signal is_empty: std_logic :='1';
begin
  empty <= is_empty;
  full <= is_full;
  num_elem<= std_logic_vector(to_unsigned(is_num_elem, 4));
  process (clk, reset) 
  begin
    if reset = '1' then
      data_out <= (others => '0');
      prev_state <= (others => '0');
      readptr <= 0;
      writeptr <= 0;
      is_num_elem <= 0;
      is_empty <= '1';
      is_full <= '0';
    elsif rising_edge(clk) then
      if enr = '1' and is_empty = '0' then  --read
        if readptr /= 0 then
          prev_state <= memory(readptr - 1);
        end if;
        data_out <= memory(readptr);
        readptr <= (readptr + 1) mod 14;
        is_num_elem <= (is_num_elem - 1) mod 14;
      end if;
      
      if enw = '1' and is_full = '0'  then  --write
      	if writeptr = 0 or data_in /= memory(writeptr - 1) then
        	memory(writeptr) <= data_in;
        	writeptr <= writeptr + 1;
        	is_num_elem <= is_num_elem + 1;
        	is_empty<='0';
        	end if;
      end if;
      end if;
      
      if readptr = 14 then   --reset readptr
        readptr <= 0;
      end if;
      
      if writeptr = 14 then  --reset writeptr
        writeptr <= 0;
      end if;
      
      if readptr = 0 then
        prev_state <= "0000";
      end if;
      
      if is_num_elem = 14 then
        is_full <= '1';
      elsif is_num_elem /= 14 then
        is_full <= '0';
      end if;
      
      if is_num_elem = 0 then
        is_empty <= '1';
      else
        is_empty <= '0';
      end if;
  end process;
end arch_fifo;

library ieee;
use ieee.std_logic_1164.all;
use ieee.numeric_std.all;

entity numarator_zecimal_reversibil is
    port (
        dir: in std_logic;
        count: out std_logic_vector(3 downto 0);
        reset: in std_logic;
        clk: in std_logic;
        load_value: in std_logic_vector(3 downto 0);
        check_destination: out std_logic;
        destination: in std_logic_vector(3 downto 0);
        enable: in std_logic_vector(3 downto 0);
        om: in std_logic;
        sg: in std_logic;
        led_om: out std_logic;
        led_sg: out std_logic
    );
end entity numarator_zecimal_reversibil;

architecture arch_numarator_zecimal_reversibil of numarator_zecimal_reversibil is
    signal count_value: std_logic_vector(3 downto 0) := (others => '0');
    signal count_helper: integer range 0 to 13 := 0;
    signal counting: std_logic := '0';
    signal stop_counting: std_logic:='0';
    signal destination_new:std_logic_vector(3 downto 0):= destination;
    signal reinit : std_logic := '0';
    signal true_destination: std_logic:='0';
begin
    led_om <= om;
    led_sg <= sg;
    process(clk, reinit, reset)
    begin
    if enable >= "0000" or load_value = destination then
    	   if(load_value = "0000" and destination = "0000") then
    	   	true_destination <= '1';
        elsif reset = '1' then
            count_helper <= to_integer(unsigned(load_value));
            destination_new <= destination;
            counting <= '0'; 
        elsif rising_edge(clk) then
            if counting = '0' and dir = '1' and stop_counting = '0' and sg = '0' and om = '0' then 
                count_helper <= to_integer(unsigned(load_value));
                counting <= '1';
            elsif counting = '0' and dir = '0' and stop_counting = '0' and sg = '0' and om = '0' then 
                count_helper <= to_integer(unsigned(load_value));
                counting <= '1';
            elsif counting = '1' and stop_counting = '0' then
            
                if dir = '1' then 
                	if count_helper >= 13 then
            			count_helper <= 0;
            		else
                    count_helper <= (count_helper + 1); --incrementare
                    end if;
                else
                	if count_helper < 0 then
                		count_helper <= 13;
                	else
                    count_helper <= (count_helper - 1); --decrementare
                    end if;
                end if;
             if(dir='1') then
                if count_helper = to_integer(unsigned(destination_new))-1 then
                	counting <= '0';
                    stop_counting <= '1'; -- Oprire numărător
                    true_destination <= '1';
                end if;
                elsif count_helper = to_integer(unsigned(destination_new))+1 then
             		counting <= '0';
                    stop_counting <= '1'; -- Oprire numărător
                    true_destination <= '1';
                 else true_destination<= '0';
                end if;
            end if;
        end if;
    if(destination_new /= destination) then
	    stop_counting <= '0';
	    destination_new<=destination;
	    reinit <= '1';
	    true_destination <='0';
    end if;
    end if;
    count <= std_logic_vector(to_unsigned(count_helper, 4));
    check_destination<=true_destination;
    end process;
   
end arch_numarator_zecimal_reversibil;

library ieee;
use ieee.std_logic_1164.all;

entity comparator is
    port (
        A, B: in std_logic_vector(3 downto 0);
        output: out std_logic
    );
end entity comparator;

architecture arch_comparator of comparator is
begin
    output<='1' when A>B else '0';
end arch_comparator;

LIBRARY ieee;
USE ieee.std_logic_1164.all;

ENTITY seven_segment_2_digits IS
  PORT (
  	input: in std_logic_vector(3 downto 0);
  	anod: out std_logic_vector(3 downto 0);
  	catod: out std_logic_vector(6 downto 0);
  	clock: in std_logic;
  	dir: in std_logic
    );
END entity seven_segment_2_digits;

ARCHITECTURE arch_seven_segment_2_digits OF seven_segment_2_digits IS

component digit_transform IS
PORT (
       etaj: in std_logic_vector(3 downto 0);
  	  c1, c2: out std_logic_vector(3 downto 0)
);
END component digit_transform;
component counter IS
PORT (
  clk: in std_logic;
  output_c: out std_logic_vector (1 downto 0)
);
END component counter;
component MUX is
port(	
	sel1, sel2: in std_logic;
	input0, input1, input2, input3: in std_logic_vector (3 downto 0);
	output_m: out std_logic_vector(3 downto 0)
);
end component MUX;
component bcd_to_7segm IS
  PORT (
	uni: in std_logic_vector(3 downto 0);
	ssd_uni: out std_logic_Vector(6 downto 0)
    );
END component bcd_to_7segm;
component mux_initializat IS
  PORT (
 	sel1, sel2: in std_logic;
 	output_m: out std_logic_vector(3 downto 0)
    );
END component mux_initializat;
component decizie_directie is
port(
	dir: in std_logic;
	output_directie: out std_logic_vector(3 downto 0)
);
end component decizie_directie;
---semnale intermediare
signal z, u: std_logic_vector(3 downto 0);
signal iesire_num: std_logic_vector(1 downto 0);
signal iesire_mux1: std_logic_vector(3 downto 0);
signal sageata_sus: std_logic_vector(3 downto 0):="1010";
signal sageata_jos: std_logic_vector(3 downto 0):="1011";
signal direction: std_logic_vector(3 downto 0):= "0000";
BEGIN
iesire_numar: counter port map(clock, iesire_num);
dig_transformare: digit_transform port map(input, u, z);
decizie_dir: decizie_directie port map(dir, direction);
multiplexor1: mux port map(iesire_num(1), iesire_num(0), u, z, direction, "0000", iesire_mux1);
bcd_7segmente: bcd_to_7segm port map(iesire_mux1, catod);
mux_init: mux_initializat port map(iesire_num(1), iesire_num(0), anod);


end architecture arch_seven_segment_2_digits;

LIBRARY ieee;
USE ieee.std_logic_1164.all;
use ieee.std_logic_unsigned.all;

entity MUX is
port(	
	sel1, sel2: in std_logic;
	input0, input1, input2, input3: in std_logic_vector (3 downto 0);
	output_m: out std_logic_vector(3 downto 0)
);
end entity MUX;

architecture arch_MUX of MUX is
begin
process(sel1,sel2)
begin
if sel1='0' and sel2='0'then output_m <= input0;
elsif sel1='0' and sel2='1' then output_m <= input1;
elsif sel1='1' and sel2='0' then output_m <= input2;
elsif sel1='1' and sel2='1' then output_m <= input3;
end if;
end process;
end architecture arch_MUX;

LIBRARY ieee;
USE ieee.std_logic_1164.all;
use ieee.std_logic_unsigned.all;

ENTITY counter IS
PORT (
  clk: in std_logic;
  output_c: out std_logic_vector (1 downto 0)
 );
END entity counter;

ARCHITECTURE arch_c OF counter IS
BEGIN
	process(clk)
	variable S: std_logic_vector (15 downto 0) := "0000000000000000";
		begin
		if rising_edge(clk) then
		S := S + 1;
		end if;
	output_c <= s(1 downto 0);	
	end process;
END arch_c;


LIBRARY ieee;
USE ieee.std_logic_1164.all;

ENTITY bcd_to_7segm IS
  PORT (
	uni: in std_logic_vector(3 downto 0);
	ssd_uni: out std_logic_Vector(6 downto 0)
    );
END entity bcd_to_7segm;

ARCHITECTURE arch_bcd_to_7segm OF bcd_to_7segm IS

BEGIN

ssd_uni<="1111110" when uni=x"0" else "0110000" when uni = x"1" else "1101101" when uni = x"2" else "1111001" when uni = x"3" else "0110011" when uni = x"4"
	else "1011011" when uni = x"5" else "1011111" when uni = x"6" else "1110000" when uni = x"7" else "1111111" when uni = x"8" else "1110011" when uni = x"9" else "0100011" 
	when uni="1010" else "0011100" when uni="1011" else "0000000";

END arch_bcd_to_7segm;


LIBRARY ieee;
USE ieee.std_logic_1164.all;
USE ieee.numeric_std.ALL;

ENTITY digit_transform is
PORT (
         etaj: in std_logic_vector(3 downto 0);
  	    c1, c2: out std_logic_vector(3 downto 0)
       );
END entity digit_transform;

ARCHITECTURE arch_digit_transform OF digit_transform IS
SHARED VARIABLE N,C,D:INTEGER;
BEGIN
	PROCESS(etaj)
	begin 

		N:=to_integer(unsigned(ETAJ));
		C:= N / 10;
		D:= N mod 10;
		C1 <= std_logic_vector( to_unsigned(C, 4));
		C2 <= std_logic_vector( to_unsigned(D, 4));

end process;
end architecture arch_digit_transform;

LIBRARY ieee;
USE ieee.std_logic_1164.all;

ENTITY mux_initializat IS
  PORT (
 	sel1, sel2: in std_logic;
 	output_m: out std_logic_vector(3 downto 0)
    );
END entity mux_initializat;

ARCHITECTURE arch_mux_initializat OF mux_initializat IS
signal s0:  std_logic_vector(3 downto 0):="0001";
signal s1:  std_logic_vector(3 downto 0):="0010";
signal s2:  std_logic_vector(3 downto 0):="0100";
signal s3:  std_logic_vector(3 downto 0):="0000";
BEGIN
process(sel1, sel2)
begin
	if sel1='0' and sel2='0' then output_m <= s0;
	elsif sel1='0' and sel2='1' then output_m <= s1;
	elsif sel1='1' and sel2='0' then output_m <= s2;
	elsif sel1='1' and sel2='1' then output_m <= s3;
	end if;
end process;
END arch_mux_initializat;

LIBRARY ieee;
USE ieee.std_logic_1164.all;

entity decizie_directie is
port(
	dir: in std_logic;
	output_directie: out std_logic_vector(3 downto 0)
);
end entity decizie_directie;
architecture arch_decizie_directie of decizie_directie is
begin
	output_directie <= "1010" when dir ='1' else "1011";
end arch_decizie_directie;

LIBRARY ieee;
USE ieee.std_logic_1164.all;
use ieee.std_logic_unsigned.all;
use ieee.numeric_std.all;
use ieee.std_logic_arith.all;


ENTITY timer5_usi_deschise IS
  PORT (
  	reset5: in std_logic;
  	clk5: in std_logic;
  	enable: in std_logic;
  	output: out std_logic
    );
END entity timer5_usi_deschise;

ARCHITECTURE arch_timer5_usi_deschise OF timer5_usi_deschise IS
signal ok: std_logic:='0';
BEGIN

	process(clk5,reset5)
	variable count_helper: natural := 0;
	begin
	if enable ='1' then
			if reset5='1' then 
			count_helper := 0; 
			ok<='0';
			elsif clk5'event and clk5='1' then
				count_helper := count_helper + 1;
			elsif count_helper = 5 then
				ok<='1';
				count_helper := 0;
			elsif count_helper /=5 then ok <='0';
			end if;
	end if;
	end process;
	output<=ok;
END arch_timer5_usi_deschise;

LIBRARY ieee;
USE ieee.std_logic_1164.all;
use ieee.std_logic_unsigned.all;
use ieee.numeric_std.all;
use ieee.std_logic_arith.all;

entity divizor_frecv_timer1 is 
    port ( 
    CLK : in std_logic;
    reset: in std_logic;
    D : out std_logic
);
end entity divizor_frecv_timer1;
 
architecture arch_divizor_frecv_timer1 of divizor_frecv_timer1 is     

signal count_c: integer :=1;
signal new_clock: std_logic :='0';
signal newQ: std_logic_vector(3 downto 0);
BEGIN

process(clk, reset)
begin
	if(reset = '1') then 
		count_c <= 1;
	elsif(RISING_EDGE(clk)) then
		if(count_c = 50000000) then
			count_c <= 1;
			new_clock <= not(new_clock);
	else count_c <= count_c+1;
	end if;
	end if;
	end process;
end arch_divizor_frecv_timer1;

LIBRARY ieee;
USE ieee.std_logic_1164.all;
use ieee.std_logic_unsigned.all;
use ieee.numeric_std.all;
use ieee.std_logic_arith.all;

entity divizor_frecv_timer3 is 
    port ( 
    CLK : in std_logic;
    reset: in std_logic;
    D : out std_logic
);
end entity divizor_frecv_timer3;
 
architecture arch_divizor_frecv_timer3 of divizor_frecv_timer3 is     

signal count_c: integer :=1;
signal new_clock: std_logic :='0';
signal newQ: std_logic_vector(3 downto 0);
BEGIN

process(clk, reset)
begin
	if(reset = '1') then 
		count_c <= 1;
	elsif(RISING_EDGE(clk)) then
		if(count_c = 3 * 50000000) then
			count_c <= 1;
			new_clock <= not(new_clock);
	else count_c <= count_c+1;
	end if;
	end if;
	end process;
end arch_divizor_frecv_timer3;

LIBRARY ieee;
USE ieee.std_logic_1164.all;

ENTITY mux_sel_viteza IS
  PORT (
 	input1, input2: in std_logic;
 	s: in std_logic;
 	output: out std_logic
    );
END entity mux_sel_viteza;

ARCHITECTURE arch_mux_sel_viteza OF mux_sel_viteza IS
BEGIN

	output <= input1 when (s='0') else input2;

END arch_mux_sel_viteza;

// VHDL entity fifo, as the project stores it:
library IEEE;
use IEEE.STD_LOGIC_1164.ALL;
use IEEE.NUMERIC_STD.ALL;

entity fifo is
port(
    clk : in std_logic;
    reset : in std_logic;
    enr : in std_logic;   
    enw : in std_logic;   
    data_in : in std_logic_vector (3 downto 0);  
    ext_or_int: in std_logic;  
    data_out : out std_logic_vector(3 downto 0);    
    prev_state : out std_logic_vector(3 downto 0);   
    empty : out std_logic;
    full : out std_logic;
    num_elem: out std_logic_vector (3 downto 0)
  );
end entity fifo;

architecture arch_fifo of fifo is
  type memory_type is array (0 to 13) of std_logic_vector(3 downto 0);
  signal memory : memory_type := (others => (others => '0'));  --memory pentru fifo
  signal readptr, writeptr : integer range 0 to 14 := 0;
  signal is_num_elem: integer range 0 to 14;
  signal is_full: std_logic := '0';
  signal is_empty: std_logic :='1';
begin
  empty <= is_empty;
  full <= is_full;
  num_elem<= std_logic_vector(to_unsigned(is_num_elem, 4));
  process (clk, reset) 
  begin
  	if reset = '1' then
      	 data_out <= (others => '0');
     	 prev_state <= (others => '0');
     	 readptr <= 0;
     	 writeptr <= 0;
     	 is_num_elem <= 0;
     	 is_empty <= '1';
     	 is_full <= '0';
    elsif rising_edge(clk) then
    if enr = '1' and is_empty = '0' then  --read
    		if readptr /= 0 then
          prev_state <= memory(readptr - 1);
        	end if;
        	data_out <= memory(readptr);
        	readptr <= (readptr + 1) mod 14;
       	 is_num_elem <= (is_num_elem - 1) mod 14;
    end if;
      
    if enw = '1' and (ext_or_int='1' or ext_or_int='0') and is_full = '0'  then  --write
      	if writeptr = 0 or data_in /= memory(writeptr - 1) then
        	memory(writeptr) <= data_in;
        	writeptr <= writeptr + 1;
        	is_num_elem <= is_num_elem + 1;
        	is_empty<='0';
        	end if;
    end if;
    end if;
      
    if readptr = 14 then   --reset readptr
    		readptr <= 0;
    end if;
      
    if writeptr = 14 then  --reset writeptr
	    writeptr <= 0;
    end if;
      
    if readptr = 0 then
   	    prev_state <= "0000";
    end if;
      
    if is_num_elem = 14 then
         is_full <= '1';
    elsif is_num_elem /= 14 then
         is_full <= '0';
    end if;
      
    if is_num_elem = 0 then
   	    is_empty <= '1';
    else
         is_empty <= '0';
    end if;
    end process;
end arch_fifo;

// VHDL entity numarator_zecimal_reversibil, as the project stores it:
library ieee;
use ieee.std_logic_1164.all;
use ieee.numeric_std.all;

entity numarator_zecimal_reversibil is
    port (
        dir: in std_logic;
        count: out std_logic_vector(3 downto 0);
        reset: in std_logic;
        clk: in std_logic;
        load_value: in std_logic_vector(3 downto 0);
        check_destination: out std_logic;
        destination: in std_logic_vector(3 downto 0);
        enable: in std_logic_vector(3 downto 0);
        om: in std_logic;
        sg: in std_logic;
        led_om: out std_logic;
        led_sg: out std_logic
    );
end entity numarator_zecimal_reversibil;

architecture arch_numarator_zecimal_reversibil of numarator_zecimal_reversibil is
    signal count_value: std_logic_vector(3 downto 0) := (others => '0');
    signal count_helper: integer range 0 to 13 := 0;
    signal counting: std_logic := '0';
    signal stop_counting: std_logic:='0';
    signal destination_new:std_logic_vector(3 downto 0):= destination;
    signal reinit : std_logic := '0';
    signal true_destination: std_logic:='0';
   -- signal load_value: std_logic_vector(3 downto 0) := "0000";
begin
    led_om <= om;
    led_sg <= sg;
    process(clk, reinit, reset)
    begin
    
    if enable >= "0000" or enable = "UUUU" or load_value = destination then
    	   if(load_value = "0000" and destination = "0000") then
    	   	true_destination <= '1';
        elsif reset = '1' then
            count_helper <= to_integer(unsigned(load_value));
            destination_new <= destination;
            counting <= '0'; 
        elsif rising_edge(clk) then
            if counting = '0' and dir = '1' and stop_counting = '0' and sg = '0' and om = '0' then 
                count_helper <= to_integer(unsigned(load_value));
                counting <= '1';
            elsif counting = '0' and dir = '0' and stop_counting = '0' and sg = '0' and om = '0' then 
                count_helper <= to_integer(unsigned(load_value));
                counting <= '1';
            elsif counting = '1' and stop_counting = '0' then
            
                if dir = '1' then 
                	if count_helper >= 13 then
            			count_helper <= 0;
            		else
                    count_helper <= (count_helper + 1); --incrementare
                    end if;
                else
                	if count_helper < 0 then
                		count_helper <= 13;
                	else
                    count_helper <= (count_helper - 1); --decrementare
                    end if;
                end if;
             if(dir='1') then
                if count_helper = to_integer(unsigned(destination_new))-1 then
                	counting <= '0';
                    stop_counting <= '1'; -- Oprire numărător
                    true_destination <= '1';
                end if;
                elsif count_helper = to_integer(unsigned(destination_new))+1 then
             		counting <= '0';
                    stop_counting <= '1'; -- Oprire numărător
                    true_destination <= '1';
                 else true_destination<= '0';
                end if;
            end if;
        end if;
    if(destination_new /= destination) then
	    stop_counting <= '0';
	    destination_new<=destination;
	    reinit <= '1';
	    true_destination <='0';
    end if;
    end if;
    count <= std_logic_vector(to_unsigned(count_helper, 4));
    check_destination<=true_destination;
   -- load_value<=load_value_t;
    end process;
   
end arch_numarator_zecimal_reversibil;

// VHDL entity comparator, as the project stores it:
library ieee;
use ieee.std_logic_1164.all;

entity comparator is
    port (
        A, B: in std_logic_vector(3 downto 0);
        output: out std_logic
    );
end entity comparator;

architecture arch_comparator of comparator is
begin
    output<='1' when A>B else '0';
end arch_comparator;

// VHDL entity seven_segment_2_digits, as the project stores it:
LIBRARY ieee;
USE ieee.std_logic_1164.all;

ENTITY seven_segment_2_digits IS
  PORT (
  	input: in std_logic_vector(3 downto 0);
  	anod: out std_logic_vector(3 downto 0);
  	catod: out std_logic_vector(6 downto 0);
  	clock: in std_logic;
  	dir: in std_logic
    );
END entity seven_segment_2_digits;

ARCHITECTURE arch_seven_segment_2_digits OF seven_segment_2_digits IS

component digit_transform IS
PORT (
       etaj: in std_logic_vector(3 downto 0);
  	  c1, c2: out std_logic_vector(3 downto 0)
);
END component digit_transform;
component counter IS
PORT (
  clk: in std_logic;
  output_c: out std_logic_vector (1 downto 0)
);
END component counter;
component MUX is
port(	
	sel1, sel2: in std_logic;
	input0, input1, input2, input3: in std_logic_vector (3 downto 0);
	output_m: out std_logic_vector(3 downto 0)
);
end component MUX;
component bcd_to_7segm IS
  PORT (
	uni: in std_logic_vector(3 downto 0);
	ssd_uni: out std_logic_Vector(6 downto 0)
    );
END component bcd_to_7segm;
component mux_initializat IS
  PORT (
 	sel1, sel2: in std_logic;
 	output_m: out std_logic_vector(3 downto 0)
    );
END component mux_initializat;
component decizie_directie is
port(
	dir: in std_logic;
	output_directie: out std_logic_vector(3 downto 0)
);
end component decizie_directie;
---semnale intermediare
signal z, u: std_logic_vector(3 downto 0);
signal iesire_num: std_logic_vector(1 downto 0);
signal iesire_mux1: std_logic_vector(3 downto 0);
signal sageata_sus: std_logic_vector(3 downto 0):="1010";
signal sageata_jos: std_logic_vector(3 downto 0):="1011";
signal direction: std_logic_vector(3 downto 0):= "0000";
BEGIN
iesire_numar: counter port map(clock, iesire_num);
dig_transformare: digit_transform port map(input, u, z);
decizie_dir: decizie_directie port map(dir, direction);
multiplexor1: mux port map(iesire_num(1), iesire_num(0), u, z, direction, "0000", iesire_mux1);
bcd_7segmente: bcd_to_7segm port map(iesire_mux1, catod);
mux_init: mux_initializat port map(iesire_num(1), iesire_num(0), anod);


end architecture arch_seven_segment_2_digits;

LIBRARY ieee;
USE ieee.std_logic_1164.all;
use ieee.std_logic_unsigned.all;

entity MUX is
port(	
	sel1, sel2: in std_logic;
	input0, input1, input2, input3: in std_logic_vector (3 downto 0);
	output_m: out std_logic_vector(3 downto 0)
);
end entity MUX;

architecture arch_MUX of MUX is
begin
process(sel1,sel2)
begin
if sel1='0' and sel2='0'then output_m <= input0;
elsif sel1='0' and sel2='1' then output_m <= input1;
elsif sel1='1' and sel2='0' then output_m <= input2;
elsif sel1='1' and sel2='1' then output_m <= input3;
end if;
end process;
end architecture arch_MUX;

LIBRARY ieee;
USE ieee.std_logic_1164.all;
use ieee.std_logic_unsigned.all;

ENTITY counter IS
PORT (
  clk: in std_logic;
  output_c: out std_logic_vector (1 downto 0)
 );
END entity counter;

ARCHITECTURE arch_c OF counter IS
BEGIN
	process(clk)
	variable S: std_logic_vector (15 downto 0) := "0000000000000000";
		begin
		if rising_edge(clk) then
		S := S + 1;
		end if;
	output_c <= s(1 downto 0);	
	end process;
END arch_c;


LIBRARY ieee;
USE ieee.std_logic_1164.all;

ENTITY bcd_to_7segm IS
  PORT (
	uni: in std_logic_vector(3 downto 0);
	ssd_uni: out std_logic_Vector(6 downto 0)
    );
END entity bcd_to_7segm;

ARCHITECTURE arch_bcd_to_7segm OF bcd_to_7segm IS

BEGIN

ssd_uni<="1111110" when uni=x"0" else "0110000" when uni = x"1" else "1101101" when uni = x"2" else "1111001" when uni = x"3" else "0110011" when uni = x"4"
	else "1011011" when uni = x"5" else "1011111" when uni = x"6" else "1110000" when uni = x"7" else "1111111" when uni = x"8" else "1110011" when uni = x"9" else "0100011" 
	when uni="1010" else "0011100" when uni="1011" else "0000000";

END arch_bcd_to_7segm;


LIBRARY ieee;
USE ieee.std_logic_1164.all;
USE ieee.numeric_std.ALL;

ENTITY digit_transform is
PORT (
         etaj: in std_logic_vector(3 downto 0);
  	    c1, c2: out std_logic_vector(3 downto 0)
       );
END entity digit_transform;

ARCHITECTURE arch_digit_transform OF digit_transform IS
SHARED VARIABLE N,C,D:INTEGER;
BEGIN
	PROCESS(etaj)
	begin 

		N:=to_integer(unsigned(ETAJ));
		C:= N / 10;
		D:= N mod 10;
		C1 <= std_logic_vector( to_unsigned(C, 4));
		C2 <= std_logic_vector( to_unsigned(D, 4));

end process;
end architecture arch_digit_transform;

LIBRARY ieee;
USE ieee.std_logic_1164.all;

ENTITY mux_initializat IS
  PORT (
 	sel1, sel2: in std_logic;
 	output_m: out std_logic_vector(3 downto 0)
    );
END mux_initializat;

ARCHITECTURE arch_mux_initializat OF mux_initializat IS
signal s0:  std_logic_vector(3 downto 0):="0001";
signal s1:  std_logic_vector(3 downto 0):="0010";
signal s2:  std_logic_vector(3 downto 0):="0100";
signal s3:  std_logic_vector(3 downto 0):="0000";
BEGIN
process(sel1, sel2)
begin
	if sel1='0' and sel2='0' then output_m <= s0;
	elsif sel1='0' and sel2='1' then output_m <= s1;
	elsif sel1='1' and sel2='0' then output_m <= s2;
	elsif sel1='1' and sel2='1' then output_m <= s3;
	end if;
end process;
END arch_mux_initializat;
LIBRARY ieee;
USE ieee.std_logic_1164.all;

ENTITY seven_segment_2_digits IS
  PORT (
  	input: in std_logic_vector(3 downto 0);
  	anod: out std_logic_vector(3 downto 0);
  	catod: out std_logic_vector(6 downto 0);
  	clock: in std_logic;
  	dir: in std_logic
    );
END entity seven_segment_2_digits;

ARCHITECTURE arch_seven_segment_2_digits OF seven_segment_2_digits IS

component digit_transform IS
PORT (
       etaj: in std_logic_vector(3 downto 0);
  	  c1, c2: out std_logic_vector(3 downto 0)
);
END component digit_transform;
component counter IS
PORT (
  clk: in std_logic;
  output_c: out std_logic_vector (1 downto 0)
);
END component counter;
component MUX is
port(	
	sel1, sel2: in std_logic;
	input0, input1, input2, input3: in std_logic_vector (3 downto 0);
	output_m: out std_logic_vector(3 downto 0)
);
end component MUX;
component bcd_to_7segm IS
  PORT (
	uni: in std_logic_vector(3 downto 0);
	ssd_uni: out std_logic_Vector(6 downto 0)
    );
END component bcd_to_7segm;
component mux_initializat IS
  PORT (
 	sel1, sel2: in std_logic;
 	output_m: out std_logic_vector(3 downto 0)
    );
END component mux_initializat;
component decizie_directie is
port(
	dir: in std_logic;
	output_directie: out std_logic_vector(3 downto 0)
);
end component decizie_directie;
---semnale intermediare
signal z, u: std_logic_vector(3 downto 0);
signal iesire_num: std_logic_vector(1 downto 0);
signal iesire_mux1: std_logic_vector(3 downto 0);
signal sageata_sus: std_logic_vector(3 downto 0):="1010";
signal sageata_jos: std_logic_vector(3 downto 0):="1011";
signal direction: std_logic_vector(3 downto 0):= "0000";
BEGIN
iesire_numar: counter port map(clock, iesire_num);
dig_transformare: digit_transform port map(input, u, z);
decizie_dir: decizie_directie port map(dir, direction);
multiplexor1: mux port map(iesire_num(1), iesire_num(0), u, z, direction, "0000", iesire_mux1);
bcd_7segmente: bcd_to_7segm port map(iesire_mux1, catod);
mux_init: mux_initializat port map(iesire_num(1), iesire_num(0), anod);


end architecture arch_seven_segment_2_digits;

LIBRARY ieee;
USE ieee.std_logic_1164.all;
use ieee.std_logic_unsigned.all;

entity MUX is
port(	
	sel1, sel2: in std_logic;
	input0, input1, input2, input3: in std_logic_vector (3 downto 0);
	output_m: out std_logic_vector(3 downto 0)
);
end entity MUX;

architecture arch_MUX of MUX is
begin
process(sel1,sel2)
begin
if sel1='0' and sel2='0'then output_m <= input0;
elsif sel1='0' and sel2='1' then output_m <= input1;
elsif sel1='1' and sel2='0' then output_m <= input2;
elsif sel1='1' and sel2='1' then output_m <= input3;
end if;
end process;
end architecture arch_MUX;

LIBRARY ieee;
USE ieee.std_logic_1164.all;
use ieee.std_logic_unsigned.all;

ENTITY counter IS
PORT (
  clk: in std_logic;
  output_c: out std_logic_vector (1 downto 0)
 );
END entity counter;

ARCHITECTURE arch_c OF counter IS
BEGIN
	process(clk)
	variable S: std_logic_vector (15 downto 0) := "0000000000000000";
		begin
		if rising_edge(clk) then
		S := S + 1;
		end if;
	output_c <= s(1 downto 0);	
	end process;
END arch_c;


LIBRARY ieee;
USE ieee.std_logic_1164.all;

ENTITY bcd_to_7segm IS
  PORT (
	uni: in std_logic_vector(3 downto 0);
	ssd_uni: out std_logic_Vector(6 downto 0)
    );
END entity bcd_to_7segm;

ARCHITECTURE arch_bcd_to_7segm OF bcd_to_7segm IS

BEGIN

ssd_uni<="1111110" when uni=x"0" else "0110000" when uni = x"1" else "1101101" when uni = x"2" else "1111001" when uni = x"3" else "0110011" when uni = x"4"
	else "1011011" when uni = x"5" else "1011111" when uni = x"6" else "1110000" when uni = x"7" else "1111111" when uni = x"8" else "1110011" when uni = x"9" else "0100011" 
	when uni="1010" else "0011100" when uni="1011" else "0000000";

END arch_bcd_to_7segm;


LIBRARY ieee;
USE ieee.std_logic_1164.all;
USE ieee.numeric_std.ALL;

ENTITY digit_transform is
PORT (
         etaj: in std_logic_vector(3 downto 0);
  	    c1, c2: out std_logic_vector(3 downto 0)
       );
END entity digit_transform;

ARCHITECTURE arch_digit_transform OF digit_transform IS
SHARED VARIABLE N,C,D:INTEGER;
BEGIN
	PROCESS(etaj)
	begin 

		N:=to_integer(unsigned(ETAJ));
		C:= N / 10;
		D:= N mod 10;
		C1 <= std_logic_vector( to_unsigned(C, 4));
		C2 <= std_logic_vector( to_unsigned(D, 4));

end process;
end architecture arch_digit_transform;

LIBRARY ieee;
USE ieee.std_logic_1164.all;

ENTITY mux_initializat IS
  PORT (
 	sel1, sel2: in std_logic;
 	output_m: out std_logic_vector(3 downto 0)
    );
END mux_initializat;

ARCHITECTURE arch_mux_initializat OF mux_initializat IS
signal s0:  std_logic_vector(3 downto 0):="0001";
signal s1:  std_logic_vector(3 downto 0):="0010";
signal s2:  std_logic_vector(3 downto 0):="0100";
signal s3:  std_logic_vector(3 downto 0):="0000";
BEGIN
process(sel1, sel2)
begin
	if sel1='0' and sel2='0' then output_m <= s0;
	elsif sel1='0' and sel2='1' then output_m <= s1;
	elsif sel1='1' and sel2='0' then output_m <= s2;
	elsif sel1='1' and sel2='1' then output_m <= s3;
	end if;
end process;
END arch_mux_initializat;

LIBRARY ieee;
USE ieee.std_logic_1164.all;

entity decizie_directie is
port(
	dir: in std_logic;
	output_directie: out std_logic_vector(3 downto 0)
);
end entity decizie_directie;
architecture arch_decizie_directie of decizie_directie is
begin
	output_directie <= "1010" when dir ='1' else "1011";
end arch_decizie_directie;

LIBRARY ieee;
USE ieee.std_logic_1164.all;

entity decizie_directie is
port(
	dir: in std_logic;
	output_directie: out std_logic_vector(3 downto 0)
);
end entity decizie_directie;
architecture arch_decizie_directie of decizie_directie is
begin
	output_directie <= "1010" when dir ='1' else "1011";
end arch_decizie_directie;

// VHDL entity timer5_usi_deschise, as the project stores it:
LIBRARY ieee;
USE ieee.std_logic_1164.all;
use ieee.std_logic_unsigned.all;
use ieee.numeric_std.all;
use ieee.std_logic_arith.all;


ENTITY timer5_usi_deschise IS
  PORT (
  	reset5: in std_logic;
  	clk5: in std_logic;
  	enable: in std_logic;
  	output: out std_logic
    );
END entity timer5_usi_deschise;

ARCHITECTURE arch_timer5_usi_deschise OF timer5_usi_deschise IS
signal ok: std_logic:='0';
BEGIN

	process(clk5,reset5)
	variable count_helper: natural := 0;
	begin
	if enable ='1' then
			if reset5='1' then 
			count_helper := 0; 
			ok<='0';
			elsif clk5'event and clk5='1' then
				count_helper := count_helper + 1;
			elsif count_helper = 5 then
				ok<='1';
				count_helper := 0;
			elsif count_helper /=5 then ok <='0';
			end if;
	end if;
	end process;
	output<=ok;
END arch_timer5_usi_deschise;

// VHDL entity divizor_frecv_timer1, as the project stores it:
LIBRARY ieee;
USE ieee.std_logic_1164.all;
use ieee.std_logic_unsigned.all;
use ieee.numeric_std.all;
use ieee.std_logic_arith.all;

entity divizor_frecv_timer1 is 
    port ( CLK : in std_logic;
    D : out std_logic;
    reset: in std_logic
);
end entity divizor_frecv_timer1;
 
architecture arch_divizor_frecv_timer1 of divizor_frecv_timer1 is     

signal count_c: integer :=1;
signal new_clock: std_logic :='0';
signal newQ: std_logic_vector(3 downto 0);
BEGIN

process(clk, reset)
begin
	if(reset = '1') then 
		count_c <= 1;
	elsif(RISING_EDGE(clk)) then
		if(count_c = 50000000) then
			count_c <= 1;
			new_clock <= not(new_clock);
	else count_c <= count_c+1;
	end if;
	end if;
	end process;
end arch_divizor_frecv_timer1;

// VHDL entity divizor_frecv_timer3, as the project stores it:
LIBRARY ieee;
USE ieee.std_logic_1164.all;
use ieee.std_logic_unsigned.all;
use ieee.numeric_std.all;
use ieee.std_logic_arith.all;

entity divizor_frecv_timer3 is 
    port ( CLK : in std_logic;
    D : out std_logic;
    reset: in std_logic
);
end entity divizor_frecv_timer3;
 
architecture arch_divizor_frecv_timer3 of divizor_frecv_timer3 is     

signal count_c: integer :=1;
signal new_clock: std_logic :='0';
signal newQ: std_logic_vector(3 downto 0);
BEGIN

process(clk, reset)
begin
	if(reset = '1') then 
		count_c <= 1;
	elsif(RISING_EDGE(clk)) then
		if(count_c = 3 * 50000000) then
			count_c <= 1;
			new_clock <= not(new_clock);
	else count_c <= count_c+1;
	end if;
	end if;
	end process;
end arch_divizor_frecv_timer3;

// VHDL entity mux_sel_viteza, as the project stores it:
LIBRARY ieee;
USE ieee.std_logic_1164.all;

ENTITY mux_sel_viteza IS
  PORT (
 	input1, input2: in std_logic;
 	s: in std_logic;
 	output: out std_logic
    );
END entity mux_sel_viteza;

ARCHITECTURE arch_mux_sel_viteza OF mux_sel_viteza IS
BEGIN

	output <= input1 when (s='0') else input2;

END arch_mux_sel_viteza;
